// Logisim project COMPUTER_One.circ as structural Verilog: 4 circuits, main circuit main
module main (
);

  wire AccuOut, Add, Carry, CarryIn, Clock, FLG, IsCarry, IsZero, jmp_1_p1, jmp_1_p2, ResetAccu, RomToData,
       SetA, Sub, WriteOut, Zero;
  wire [7:0] Data, ROM;
  wire [11:8] rom_1_data;

  Counter #(.ongoal("stay")) counter_1 ();  // open: load, D, count, Q, carry, clk, clr
  // JMP jmp_1: pin names not known; wires that end beside it: jmp_1_p1, jmp_1_p2
  ROM #(.dataWidth(12)) rom_1 (.data({rom_1_data, ROM}));  // open: addr
  Decoder #(.select(4), .enable("false")) decoder_1 (.sel(rom_1_data));  // open: out0, out1, out2, out3, out4, out5, out6, out7, out8, out9, out10, out11, out12, out13, out14, out15
  FLG flg_1 (
    .FLG(FLG), .ROM(ROM), .IsCarry(IsCarry), .IsZero(IsZero), .Clock(Clock), .WriteOut(WriteOut),
    .AccuOut(AccuOut), .RomToData(RomToData), .Carry(Carry), .Zero(Zero), .Sub(Sub), .CarryIn(CarryIn),
    .ResetAccumulator(ResetAccu));
  ALU alu_1 (
    .Sub(Sub), .CarryIn(CarryIn), .Ain(Data), .SetA(SetA), .AccumulatorOut(AccuOut), .Add(Add),
    .ResetAcum(ResetAccu), .Clock(Clock), .Accumulator(Data), .AccumulatorIsZero(IsZero), .CarryOut(IsCarry));

  // Notes on the sheet:
  //   contents of rom_1 (hex, n*v repeats v):
  //   aa0 b01 f0a e00 700 a09 600 200 305 b00 c00 600 200 30d
endmodule

module JMP (
  input  JMP,
  input  JMPZERO,
  input  ZERO,
  input  JMPCARRY,
  input  CARRY,
  input  JMPDATA,
  input  JMPEQUAL,
  input  [7:0] ROM,
  input  [7:0] DATA,
  input  SetEqualREG,
  input  Clock,
  output [7:0] PCIn,
  output PCLoad
);

  wire and_1_out, and_2_out, and_3_out, comparator_1_eq;
  wire [7:0] register_1_q;

  and and_1 (and_1_out, JMPZERO, ZERO);
  and and_2 (and_2_out, JMPCARRY, CARRY);
  Register register_1 (.D(DATA), .en(SetEqualREG), .clk(Clock), .Q(register_1_q));  // open: clr
  Comparator comparator_1 (.a(DATA), .b(register_1_q), .eq(comparator_1_eq));  // open: gt, lt
  and and_3 (and_3_out, JMPEQUAL, comparator_1_eq);
  Multiplexer #(.width(8), .enable("false")) multiplexer_1 (.in0(ROM), .in1(DATA), .out(PCIn), .sel(JMPDATA));
  or or_1 (PCLoad, JMP, and_1_out, and_2_out, JMPDATA, and_3_out);
endmodule

module ALU (
  input  Sub,
  input  CarryIn,
  input  [7:0] Ain,
  input  SetA,
  input  AccumulatorOut,
  input  Add,
  input  ResetAcum,
  input  Clock,
  output [7:0] Accumulator,
  output AccumulatorIsZero,
  output CarryOut
);

  wire or_1_out;
  wire [7:0] adder_1_out, multiplexer_1_out, negator_1_out, register_1_q, register_2_q;

  Register register_1 (.D(Ain), .en(SetA), .clk(Clock), .Q(register_1_q));  // open: clr
  Negator negator_1 (.in(register_1_q), .out(negator_1_out));
  Multiplexer #(.width(8), .enable("false")) multiplexer_1 (
    .in0(register_1_q), .in1(negator_1_out), .out(multiplexer_1_out), .sel(Sub));
  Register register_2 (.D(adder_1_out), .en(Add), .clk(Clock), .Q(register_2_q), .clr(ResetAcum));
  Adder adder_1 (.a(multiplexer_1_out), .b(register_2_q), .out(adder_1_out), .cin(CarryIn), .cout(CarryOut));
  assign Accumulator = AccumulatorOut ? register_2_q : 8'bz;  // Controlled_Buffer controlled_buffer_1
  or or_1 (or_1_out, register_2_q[0], register_2_q[1], register_2_q[2], register_2_q[3], register_2_q[4], register_2_q[5], register_2_q[6], register_2_q[7]);
  not not_1 (AccumulatorIsZero, or_1_out);
endmodule

module FLG (
  input  FLG,
  input  [7:0] ROM,
  input  IsCarry,
  input  IsZero,
  input  Clock,
  output WriteOut,
  output AccuOut,
  output RomToData,
  output Carry,
  output Zero,
  output Sub,
  output CarryIn,
  output ResetAccumulator
);

  wire decoder_1_out0, decoder_1_out1, decoder_1_out2, decoder_1_out3, decoder_1_out4, decoder_1_out5,
       decoder_1_out6, decoder_1_out7, decoder_1_out8, decoder_1_out9, decoder_1_out10, decoder_1_out11;

  Decoder #(.select(4), .enable("false")) decoder_1 (
    .out0(decoder_1_out0), .out1(decoder_1_out1), .out2(decoder_1_out2), .out3(decoder_1_out3),
    .out4(decoder_1_out4), .out5(decoder_1_out5), .out6(decoder_1_out6), .out7(decoder_1_out7),
    .out8(decoder_1_out8), .out9(decoder_1_out9), .out10(decoder_1_out10), .out11(decoder_1_out11),
    .out12(ResetAccumulator), .sel(ROM[7:4]));  // open: out13, out14, out15
  S_R_Flip_Flop WriteOutf (
    .S(decoder_1_out0), .R(decoder_1_out1), .clk(Clock), .Q(WriteOut));  // open: reset, Qn, preset
  S_R_Flip_Flop AccuOutf (.S(decoder_1_out2), .R(decoder_1_out3), .clk(Clock), .Q(AccuOut));  // open: reset, Qn, preset
  S_R_Flip_Flop RomToDataf (
    .S(decoder_1_out4), .R(decoder_1_out5), .clk(Clock), .Q(RomToData));  // open: reset, Qn, preset
  S_R_Flip_Flop Carryf (.S(IsCarry), .R(decoder_1_out6), .clk(Clock), .Q(Carry));  // open: reset, Qn, preset
  S_R_Flip_Flop Zerof (.S(IsZero), .R(decoder_1_out7), .clk(Clock), .Q(Zero));  // open: reset, Qn, preset
  S_R_Flip_Flop Subf (.S(decoder_1_out8), .R(decoder_1_out9), .clk(Clock), .Q(Sub));  // open: reset, Qn, preset
  S_R_Flip_Flop CarryInf (
    .S(decoder_1_out10), .R(decoder_1_out11), .clk(Clock), .Q(CarryIn));  // open: reset, Qn, preset
endmodule
